# Fritzing sketch Police Lights (saved by Fritzing 0.9.4)
breadboards: 1

parts:
  Part1 = Arduino Ethernet Shield (Rev3)
  LED2 = smd LED [color="Blue (505nm)" package="1206 [SMD]"]
  LED3 = LED - 5mm [color="Red (633nm)" package="5 mm [THT]"]
  LED4 = LED - 5mm [color="Blue (505nm)" package="5 mm [THT]"]
  LED5 = LED - 5mm [color="Red (633nm)" package="5 mm [THT]"]
  R1 = Resistor [tolerance=±5% resistance=220 package=THT]
  R2 = Resistor [tolerance=±5% resistance=220 package=THT]
  R3 = Resistor [tolerance=±5% resistance=220 package=THT]
  R4 = Resistor [tolerance=±5% resistance=220 package=THT]
  S1 = Momentary Switch [package=ksa_sealed_tac_switch]
  S2 = Momentary Switch [package=ksa_sealed_tac_switch]
  J1 = Piezo Speaker

nets:
  N1: Part1.D8, LED2.anode
  N2: Part1.PWM_D9, LED5.anode
  N3: Part1.ETH_CS, LED3.anode
  N4: Part1.PWM_D11, LED4.anode
  N5: Part1.GND, R1.Pin_1, R2.Pin_1, R3.Pin_1, R4.Pin_1, J1.pin1
  N6: Part1.D7, J1.pin2
  N7: LED2.cathode, R1.Pin_0
  N8: LED3.cathode, R2.Pin_0
  N9: LED4.cathode, R4.Pin_0
  N10: LED5.cathode, R3.Pin_0
  N11: S1.1, S1.2
  N12: S1.3, S1.4
  N13: S2.1, S2.2
  N14: S2.3, S2.4
